# Fritzing sketch Wiring_Diagram (saved by Fritzing 0.9.10b)
breadboards: 1

parts:
  Processor = Arduino Mega 2560 (Rev3)
  Part2 = InvenSense MPU6050
  VCC1 = Battery block 9V
  U1 = Voltage Regulator [package=to220-adj]
  U2 = HALL-EFFECT [package=sc70]
  U3 = HALL-EFFECT [package=sc70]
  U4 = HALL-EFFECT [package=sc70]
  U5 = HALL-EFFECT [package=sc70]
  VCC2 = Battery block 9V
  Horn = Momentary Switch [package=tactile_switch_smd]
  R1 = Resistor [tolerance=±5% power=0.25 resistance=220 package=THT]

nets:
  N1: Processor.D21/SCL, Processor.SCL, Part2.SCL
  N2: Processor.D20/SDA, Processor.SDA, Part2.SDA
  N3: Processor.D19/RX1, Part2.INT
  N4: Processor.D15/RX3, R1.Pin_1
  GND: Processor.GND, Part2.GND, U1.ADJ, U2.GND, U3.GND, U4.GND, U5.GND
  N5: Processor.D13_PWM, U2.OUT
  N6: Processor.D12_PWM, U3.OUT
  N7: Processor.D11_PWM, U4.OUT
  N8: Processor.D10_PWM, U5.OUT
  VCC: Part2.VCC, U1.OUT, U2.VCC, U3.VCC, U4.VCC, U5.VCC, Horn.2
  GND_2: VCC1.-, VCC2.-
  N9: VCC1.+, U1.IN, VCC2.+
  N10: Horn.4, R1.Pin_0
